# Fritzing sketch RGBTouch (saved by Fritzing 0.9.3b)
circuit board: 6.88566cm x 5.36311cm

parts:
  Arduino1 = Arduino Uno (Rev3)
  R1 = Resistor [tolerance=±5% resistance=220 package=THT]
  R2 = Resistor [tolerance=±5% resistance=220 package=THT]
  R3 = Resistor [tolerance=±5% resistance=220 package=THT]
  LED1 = RGB LED (com. cathode, rgb) [package="5 mm [THT]"]
  J1 = female pin header, 1 pin [form="♀ (female)"]
  J2 = female pin header, 1 pin [form="♀ (female)"]
  J3 = female pin header, 1 pin [form="♀ (female)"]

nets:
  N1: Arduino1.A0, J1.pin1
  N2: Arduino1.A1, J2.pin1
  N3: Arduino1.A2, J3.pin1
  N4: Arduino1.D9_PWM, R1.Pin_0
  N5: Arduino1.D10_PWM/SS, R2.Pin_0
  N6: Arduino1.D11_PWM/MOSI, R3.Pin_0
  N7: Arduino1.GND, LED1.common_cathode
  N8: R1.Pin_1, LED1.red_anode
  N9: R2.Pin_1, LED1.green_anode
  N10: R3.Pin_1, LED1.blue_anode

notes:
  Cambiá los colores del led con solo acercar tus manos a los cables!

// code stored in the sketch: RGBTouch.ino
/*
 /*
  RGBTouch
  Controla el color de un led RGB conectado a los pines 9,10 y 11, acercando o
  alejando la mano a 3 cables conectados a A0, A1 y A2.
  El circuito:
  * 3 cables de 20 cm aprox.
  * 3 resistencias de 220 ohm, para limitar la corriente del led
  * 1 led rgb de 5mm, cátodo común (-)

  Creado el 24 de abril de 2017
  Por derfaq

*/

#include <Arduino.h>
#include <ADCTouch.h>

#define LED_R 9
#define LED_G 10
#define LED_B 11

int refR, refG, refB;

void setup(){

  Serial.begin(9600); //Apertura del puerto serie para debugging

  pinMode(LED_R,OUTPUT); //Configuracion de los pines conectados al led
  pinMode(LED_G,OUTPUT);
  pinMode(LED_B,OUTPUT);

  refR = ADCTouch.read(A0,500); //Crea el valor de referencia al inicio del programa
  refG = ADCTouch.read(A1,500); //para cada canal, correspondiente a cada color
  refB = ADCTouch.read(A2,500);

}

void loop(){
  int valueR = ADCTouch.read(A0); //Lectura continua de los pines analógicos
  int valueG = ADCTouch.read(A1); //ADCTouch.read() *sin segundo parámetro
  int valueB = ADCTouch.read(A2);

  valueR -= refR; //Remueve el offset, es decir hace la diferencia con el valor al
                  //inicio del programa
  valueG -= refG;
  valueB -= refB;

  Serial.print("R| "); //Envio de los valores
  Serial.print(valueR);
  Serial.print(" G| ");
  Serial.print(valueG);
  Serial.print(" B| ");
  Serial.println(valueB);

  /* En mi Funduino chino viejo y querido, el valor para un trozo de cable
    de par telefónico, aislado, de aproximadamente 10cm, varía aproximadamente
    entre 0 y 200 cuando acerco la mano, y cuando apreto más, alrededor de 270.
    Estos valores resultan muy prácticos para el analogWrite();
    Otra observación, es que se produce interferencia entre los pines. Así,
    a medida que me acerco mas al canal rojo (A0), empiezan a aparecer valores en
    el canal verde (A1) y en menor medida en el canal azul (A2).
  */

  if(valueR<2){valueR = 0;} //Si el valor es menor que 2, considero que no hay cambio
  valueR = constrain(valueR,0,255); //luego restrinjo los valores entre 0..255
  if(valueG<2){valueG = 0;}
  valueG = constrain(valueG,0,255);
  if(valueB<2){valueB = 0;}
  valueB = constrain(valueB,0,255);

  analogWrite(LED_R,valueR); //Enciedo el led rgb con los valores correspondientes
  analogWrite(LED_G,valueG);
  analogWrite(LED_B,valueB);
}
